// Logisim project AtlasArch.circ as structural Verilog: 1 circuit, main circuit main
module main (
);

  wire ADD_out, and_1_out, and_3_out, and_4_out, and_5_out, and_6_out, and_7_out, and_8_out, and_9_out,
       and_10_out, clock_1_out, d_ff_1_q, d_ff_1_qn, LDR1_out, LDR2_out, LDR3_out, LDR4_out, LDR_out,
       not_1_out, not_2_out, not_3_out, not_5_out, not_6_out, not_7_out, not_8_out, not_9_out, not_10_out,
       not_11_out, not_12_out, not_13_out, One_out, or_2_out, or_3_out, or_4_out, Reg1_out, Reg2_out,
       Reg3_out, Reg4_out, Rone_out, STR_out, SUB_out, Three_out, Two_out, undriven;
  wire [5:0] Instruction_q;
  wire [9:0] adder_2_out, controlled_buffer_3_out, controlled_buffer_4_out, controlled_buffer_6_out,
       controlled_buffer_7_out, controlled_buffer_11_out, controlled_buffer_14_out, controlled_buffer_16_out,
       Instruction_q_3, R1_q, R2_q, R3_q, R4_q, ram_1_dout, subtractor_1_out;
  wire [15:0] adder_1_out, controlled_buffer_1_out, Instruction_q_2, PC_q;
  wire [31:0] rom_1_data;

  not not_1 (not_1_out, d_ff_1_q);
  D_Flip_Flop d_ff_1 (.D(not_1_out), .clk(clock_1_out), .Q(d_ff_1_q), .Qn(d_ff_1_qn));  // open: preset, reset
  Clock clock_1 (.out(clock_1_out));
  Register #(.width(32)) Instruction (
    .D(rom_1_data), .en(d_ff_1_qn), .clk(clock_1_out), .Q({Instruction_q_3, Instruction_q_2, Instruction_q}));  // open: clr
  not not_2 (not_2_out, and_1_out);
  assign controlled_buffer_1_out = not_2_out ? adder_1_out : 16'bz;  // Controlled_Buffer controlled_buffer_1
  Register #(.width(16)) PC (.D(controlled_buffer_1_out), .en(d_ff_1_qn), .clk(d_ff_1_qn), .Q(PC_q));  // open: clr
  assign controlled_buffer_1_out = and_1_out ? Instruction_q_2 : 16'bz;  // Controlled_Buffer controlled_buffer_2
  Adder #(.width(16)) adder_1 (.a(16'h1), .b(PC_q), .out(adder_1_out));  // open: cin, cout
  ROM #(.addrWidth(16), .dataWidth(32)) rom_1 (.addr(PC_q), .data(rom_1_data));
  and and_1 (and_1_out, Instruction_q[0], Instruction_q[1], Instruction_q[2], Instruction_q[3], Instruction_q[4], Instruction_q[5]);
  Register #(.width(10)) R1 (.D(ram_1_dout), .en(Rone_out), .clk(d_ff_1_qn), .Q(R1_q));  // open: clr
  Register #(.width(10)) R3 (.D(ram_1_dout), .en(or_2_out), .clk(d_ff_1_qn), .Q(R3_q));  // open: clr
  Register #(.width(10)) R2 (.D(ram_1_dout), .en(or_3_out), .clk(d_ff_1_qn), .Q(R2_q));  // open: clr
  Register #(.width(10)) R4 (.D(controlled_buffer_3_out), .en(undriven), .clk(d_ff_1_qn), .Q(R4_q));  // open: clr
  or Rone (Rone_out, Reg1_out, LDR1_out);
  assign controlled_buffer_3_out = undriven ? controlled_buffer_16_out : 10'bz;  // Controlled_Buffer controlled_buffer_3
  or or_1 (Instruction_q[5], Reg4_out, LDR4_out);
  or or_2 (or_2_out, Reg3_out, LDR3_out);
  and LDR1 (LDR1_out, LDR_out, One_out);
  and LDR2 (LDR2_out, LDR_out, Two_out);
  and LDR3 (LDR3_out, LDR_out, Three_out);
  and LDR4 (LDR4_out, LDR_out, Instruction_q[5]);
  // AND_Gate JMPE is placed but not wired
  // AND_Gate JMPNE is placed but not wired
  // AND_Gate JMPGREAT is placed but not wired
  // AND_Gate JMPLESS is placed but not wired
  or or_3 (or_3_out, Reg2_out, LDR2_out);
  // AND_Gate and_2 is placed but not wired
  and Reg1 (Reg1_out, Instruction_q[0], Instruction_q[3]);
  and Reg2 (Reg2_out, Instruction_q[0], Instruction_q[4]);
  and Reg3 (Reg3_out, Instruction_q[0], Instruction_q[5]);
  and Reg4 (Reg4_out, Instruction_q[0], and_3_out);
  and and_3 (and_3_out, Instruction_q[4], Instruction_q[5]);
  and LDR (LDR_out, Instruction_q[0], Instruction_q[1]);
  and STR (STR_out, Instruction_q[0], Instruction_q[2], not_3_out);
  not not_3 (not_3_out, Instruction_q[5]);
  RAM #(.addrWidth(16), .dataWidth(10)) ram_1 (
    .we(STR_out), .oe(LDR_out), .clk(d_ff_1_qn), .din(Instruction_q_3), .dout(ram_1_dout));  // open: addr
  and One (One_out, not_5_out, Instruction_q[2]);
  and Two (Two_out, not_6_out, Instruction_q[4]);
  and Three (Three_out, Instruction_q[4], Instruction_q[2]);
  and and_4 (and_4_out, Instruction_q[2], Instruction_q[3]);
  // NOT_Gate not_4 has open pins: in=and_4_out, out=open
  not not_5 (not_5_out, Instruction_q[4]);
  not not_6 (not_6_out, Instruction_q[2]);
  not not_7 (not_7_out, Instruction_q_2[3]);
  not not_8 (not_8_out, Instruction_q_2[2]);
  assign controlled_buffer_4_out = Instruction_q_2[0] ? Instruction_q_2[15:6] : 10'bz;  // Controlled_Buffer controlled_buffer_4
  assign controlled_buffer_4_out = not_9_out ? controlled_buffer_7_out : 10'bz;  // Controlled_Buffer controlled_buffer_5
  assign controlled_buffer_6_out = Instruction_q_2[1] ? Instruction_q_3 : 10'bz;  // Controlled_Buffer controlled_buffer_6
  not not_9 (not_9_out, Instruction_q_2[0]);
  assign controlled_buffer_7_out = and_5_out ? R1_q : 10'bz;  // Controlled_Buffer controlled_buffer_7
  and and_5 (and_5_out, Instruction_q_2[2], not_7_out);
  assign controlled_buffer_7_out = and_6_out ? R3_q : 10'bz;  // Controlled_Buffer controlled_buffer_8
  and and_6 (and_6_out, Instruction_q_2[3], not_8_out);
  assign controlled_buffer_7_out = and_7_out ? R2_q : 10'bz;  // Controlled_Buffer controlled_buffer_9
  and and_7 (and_7_out, Instruction_q_2[2], Instruction_q_2[3]);
  assign controlled_buffer_6_out = not_10_out ? controlled_buffer_11_out : 10'bz;  // Controlled_Buffer controlled_buffer_10
  not not_10 (not_10_out, Instruction_q_2[1]);
  assign controlled_buffer_11_out = and_8_out ? R1_q : 10'bz;  // Controlled_Buffer controlled_buffer_11
  and and_8 (and_8_out, Instruction_q_2[4], not_11_out);
  not not_11 (not_11_out, Instruction_q_2[5]);
  assign controlled_buffer_11_out = and_9_out ? R3_q : 10'bz;  // Controlled_Buffer controlled_buffer_12
  and and_9 (and_9_out, Instruction_q_2[5], not_12_out);
  assign controlled_buffer_11_out = and_10_out ? R2_q : 10'bz;  // Controlled_Buffer controlled_buffer_13
  not not_12 (not_12_out, Instruction_q_2[4]);
  and and_10 (and_10_out, Instruction_q_2[5], Instruction_q_2[5]);
  not not_13 (not_13_out, Instruction_q[2]);
  Adder #(.width(10)) adder_2 (
    .a(controlled_buffer_4_out), .b(controlled_buffer_6_out), .out(adder_2_out));  // open: cin, cout
  and ADD (ADD_out, not_13_out, Instruction_q[3], Instruction_q[4], Instruction_q[5]);
  assign controlled_buffer_14_out = ADD_out ? adder_2_out : 10'bz;  // Controlled_Buffer controlled_buffer_14
  and SUB (SUB_out, Instruction_q[2], Instruction_q[3], Instruction_q[4], Instruction_q[5]);
  Subtractor #(.width(10)) subtractor_1 (
    .a(controlled_buffer_4_out), .b(controlled_buffer_6_out), .out(subtractor_1_out));  // open: bin, bout
  assign controlled_buffer_14_out = SUB_out ? subtractor_1_out : 10'bz;  // Controlled_Buffer controlled_buffer_15
  or or_4 (or_4_out, SUB_out, ADD_out);
  Comparator #(.width(10)) comparator_1 (.a(controlled_buffer_4_out), .b(controlled_buffer_6_out));  // open: gt, eq, lt
  assign controlled_buffer_16_out = or_4_out ? controlled_buffer_14_out : 10'bz;  // Controlled_Buffer controlled_buffer_16
  // AND_Gate CMP is placed but not wired
  // AND_Gate and_11 is placed but not wired
  // AND_Gate and_12 is placed but not wired
endmodule
